// Logisim project CPU.circ as structural Verilog: 11 circuits, main circuit main
module main (
);

  wire clock_1_p1, clock_1_p2, clock_1_p3, clock_1_p4, clock_1_p5, clock_1_p6, clock_1_p7, clock_1_p10,
       clock_1_p11, clock_1_p15, controlled_buffer_1_out, not_1_out, pin_1_p1, pin_1_p2, pin_2_p1, pin_2_p2,
       pin_3_p1, pin_3_p3, pin_3_p7, pin_3_p9, pin_5_p11, pin_6_p1, pin_8_p1, pin_8_p3, pin_8_p5,
       splitter_1_p1, splitter_1_p2, splitter_1_p3, splitter_1_p4, splitter_1_p5, splitter_1_p6,
       splitter_1_p7, splitter_1_p8, splitter_1_p9, splitter_1_p10, splitter_1_p11, splitter_1_p12,
       splitter_2_p1, splitter_2_p2, splitter_2_p3, splitter_2_p4, splitter_2_p27, splitter_3_p2,
       splitter_4_p1, splitter_4_p3, splitter_5_p14, splitter_5_p18, splitter_6_p6, splitter_6_p12,
       splitter_8_p1, splitter_9_p18, splitter_10_p14, splitter_12_p1, splitter_12_p3, undriven;
  wire [11:0] pin_6_p3, splitter_1_p13, splitter_1_p14, splitter_3_p1, splitter_3_p3, splitter_5_p13,
       splitter_5_p15, splitter_7_p1, splitter_7_p2;
  wire [15:0] controlled_buffer_3_out, controlled_buffer_4_out, controlled_buffer_7_out,
       controlled_buffer_9_out, controlled_buffer_11_out, controlled_buffer_12_out, controlled_buffer_13_out,
       ram_1_data, splitter_2_p26, splitter_4_p7, splitter_6_p11, splitter_8_p5, splitter_9_p15,
       splitter_9_p16, splitter_10_p13, splitter_11_p1, splitter_12_p7, splitter_13_p17;

  // Pin pin_1: pin names not known; wires that end beside it: pin_1_p1, pin_1_p2, pin_1_p2
  // Pin pin_2: pin names not known; wires that end beside it: pin_2_p1, pin_2_p2, pin_2_p1
  ALU1 alu1_1 ();
  assign controlled_buffer_1_out = not_1_out ? clock_1_p7 : 1'bz;  // Controlled_Buffer controlled_buffer_1
  // Clock clock_1: pin names not known; wires that end beside it: clock_1_p1, clock_1_p2, clock_1_p3, clock_1_p4, clock_1_p5, clock_1_p6, clock_1_p7, controlled_buffer_1_out, clock_1_p1, clock_1_p10, clock_1_p11, clock_1_p1, clock_1_p10, clock_1_p11, clock_1_p15
  not not_1 (not_1_out, clock_1_p15);
  // Splitter splitter_1: pin names not known; wires that end beside it: splitter_1_p1, splitter_1_p2, splitter_1_p3, splitter_1_p4, splitter_1_p5, splitter_1_p6, splitter_1_p7, splitter_1_p8, splitter_1_p9, splitter_1_p10, splitter_1_p11, splitter_1_p12, splitter_1_p13, splitter_1_p14
  CLOCK clock_2 ();
  assign splitter_1_p14 = pin_3_p7 ? splitter_1_p13 : 12'bz;  // Controlled_Buffer controlled_buffer_2
  // Pin pin_3: pin names not known; wires that end beside it: pin_3_p1, pin_1_p2, pin_3_p3, clock_1_p1, pin_3_p1, pin_3_p3, pin_3_p7, pin_3_p7, pin_3_p9, pin_3_p9
  AC ac_1 ();
  assign controlled_buffer_3_out = splitter_2_p27 ? splitter_2_p26 : 16'bz;  // Controlled_Buffer controlled_buffer_3
  // Splitter splitter_2: pin names not known; wires that end beside it: splitter_2_p1, splitter_2_p2, splitter_2_p3, splitter_2_p4, splitter_1_p1, splitter_1_p2, splitter_1_p3, splitter_1_p4, splitter_1_p5, splitter_1_p6, splitter_1_p7, splitter_1_p8, clock_1_p1, splitter_1_p9, splitter_1_p10, splitter_1_p11, clock_1_p2, clock_1_p3, clock_1_p4, clock_1_p5, clock_1_p6, splitter_1_p12, controlled_buffer_3_out, pin_2_p1, pin_2_p1, splitter_2_p26, splitter_2_p27, splitter_2_p27, pin_1_p1
  PC pc_1 ();
  assign controlled_buffer_4_out = splitter_4_p1 ? splitter_4_p7 : 16'bz;  // Controlled_Buffer controlled_buffer_4
  // Splitter splitter_3: pin names not known; wires that end beside it: splitter_3_p1, splitter_3_p2, splitter_3_p3, splitter_1_p1, splitter_1_p2, splitter_1_p3
  assign splitter_3_p3 = pin_3_p9 ? splitter_3_p1 : 12'bz;  // Controlled_Buffer controlled_buffer_5
  // Splitter splitter_4: pin names not known; wires that end beside it: splitter_4_p1, splitter_4_p1, splitter_4_p3, clock_1_p1, controlled_buffer_4_out, splitter_4_p3, splitter_4_p7, splitter_2_p1, splitter_2_p2, splitter_2_p3, splitter_2_p4, splitter_1_p1, splitter_1_p2, splitter_1_p3, splitter_1_p4, splitter_1_p5, splitter_1_p6, splitter_1_p7, splitter_1_p8, splitter_1_p9, splitter_1_p10
  // Pin pin_4: pin names not known; wires that end beside it: splitter_1_p4, splitter_3_p2, splitter_1_p5, splitter_1_p6, splitter_1_p7, splitter_1_p8, splitter_1_p9, splitter_1_p10, splitter_1_p11, splitter_1_p12
  // Pin pin_5: pin names not known; wires that end beside it: splitter_1_p11, splitter_1_p12, splitter_2_p1, splitter_2_p2, splitter_2_p3, splitter_2_p4, splitter_1_p1, splitter_1_p2, splitter_1_p3, splitter_1_p4, pin_5_p11, splitter_1_p5, splitter_1_p6, splitter_1_p7
  // Splitter splitter_5: pin names not known; wires that end beside it: splitter_1_p1, splitter_1_p2, splitter_1_p3, splitter_1_p4, splitter_1_p5, splitter_1_p6, splitter_1_p7, splitter_1_p8, splitter_1_p9, splitter_1_p10, splitter_1_p11, splitter_1_p12, splitter_5_p13, splitter_5_p14, splitter_5_p15, clock_1_p1, splitter_5_p14, splitter_5_p18, splitter_5_p18
  assign splitter_5_p15 = splitter_5_p18 ? splitter_5_p13 : 12'bz;  // Controlled_Buffer controlled_buffer_6
  assign controlled_buffer_7_out = splitter_6_p12 ? splitter_6_p11 : 16'bz;  // Controlled_Buffer controlled_buffer_7
  // Splitter splitter_6: pin names not known; wires that end beside it: splitter_1_p8, splitter_1_p9, splitter_1_p10, splitter_1_p11, splitter_1_p12, splitter_6_p6, controlled_buffer_7_out, pin_5_p11, pin_5_p11, splitter_6_p6, splitter_6_p11, splitter_6_p12, splitter_6_p12
  AR ar_1 ();
  IR ir_1 ();
  // Splitter splitter_7: pin names not known; wires that end beside it: splitter_7_p1, splitter_7_p2, splitter_1_p1, splitter_1_p2, splitter_1_p3, splitter_1_p4, splitter_1_p5, splitter_1_p6, splitter_1_p7, splitter_1_p8, splitter_1_p9, splitter_1_p10, splitter_1_p11, splitter_1_p12, splitter_2_p1, splitter_2_p2
  assign splitter_7_p2 = pin_6_p1 ? splitter_7_p1 : 12'bz;  // Controlled_Buffer controlled_buffer_8
  // Pin pin_6: pin names not known; wires that end beside it: pin_6_p1, pin_6_p1, pin_6_p3, pin_6_p3
  CU cu_1 ();
  assign controlled_buffer_9_out = splitter_8_p1 ? splitter_8_p5 : 16'bz;  // Controlled_Buffer controlled_buffer_9
  // Splitter splitter_8: pin names not known; wires that end beside it: splitter_8_p1, splitter_8_p1, clock_1_p1, controlled_buffer_9_out, splitter_8_p5, splitter_2_p1, splitter_2_p2, splitter_2_p3, splitter_2_p4, splitter_1_p1, splitter_1_p2, splitter_1_p3, splitter_1_p4, splitter_1_p5, splitter_1_p6, splitter_1_p7, splitter_1_p8
  // Pin pin_7: pin names not known; wires that end beside it: splitter_1_p9, splitter_1_p10, splitter_1_p11, splitter_1_p12, splitter_2_p1, pin_2_p2, splitter_2_p2, splitter_2_p3, splitter_2_p4, splitter_1_p1, splitter_1_p2, splitter_1_p3
  // Splitter splitter_9: pin names not known; wires that end beside it: splitter_2_p3, splitter_2_p4, splitter_1_p1, splitter_1_p2, splitter_1_p3, splitter_1_p4, splitter_1_p5, splitter_1_p6, splitter_1_p7, splitter_1_p8, splitter_1_p9, splitter_1_p10, splitter_1_p11, splitter_1_p12, splitter_9_p15, splitter_9_p16, clock_1_p1, splitter_9_p18, splitter_9_p18
  assign splitter_9_p16 = splitter_9_p18 ? splitter_9_p15 : 16'bz;  // Controlled_Buffer controlled_buffer_10
  assign controlled_buffer_11_out = splitter_10_p14 ? splitter_10_p13 : 16'bz;  // Controlled_Buffer controlled_buffer_11
  // Splitter splitter_10: pin names not known; wires that end beside it: splitter_1_p4, splitter_1_p5, splitter_1_p6, splitter_1_p7, splitter_1_p8, splitter_1_p9, splitter_1_p10, splitter_1_p11, splitter_1_p12, controlled_buffer_11_out, pin_2_p2, pin_2_p2, splitter_10_p13, splitter_10_p14, splitter_10_p14
  assign controlled_buffer_12_out = pin_8_p1 ? splitter_11_p1 : 16'bz;  // Controlled_Buffer controlled_buffer_12
  TMP tmp_1 ();
  DR dr_1 ();
  // Splitter splitter_11: pin names not known; wires that end beside it: splitter_11_p1, controlled_buffer_12_out, splitter_2_p1, splitter_2_p2, splitter_2_p3, splitter_2_p4, splitter_1_p1, splitter_1_p2, splitter_1_p3, splitter_1_p4, splitter_1_p5, splitter_1_p6, splitter_1_p7, splitter_1_p8, splitter_1_p9, splitter_1_p10, splitter_1_p11, splitter_1_p12
  // Pin pin_8: pin names not known; wires that end beside it: pin_8_p1, pin_8_p1, pin_8_p3, pin_8_p3, pin_8_p5
  assign controlled_buffer_13_out = splitter_12_p1 ? splitter_12_p7 : 16'bz;  // Controlled_Buffer controlled_buffer_13
  // Splitter splitter_12: pin names not known; wires that end beside it: splitter_12_p1, splitter_12_p1, splitter_12_p3, clock_1_p1, controlled_buffer_13_out, splitter_12_p3, splitter_12_p7, splitter_2_p1, splitter_2_p2, splitter_2_p3, splitter_2_p4, splitter_1_p1, splitter_1_p2, splitter_1_p3, splitter_1_p4, splitter_1_p5, splitter_1_p6, splitter_1_p7, splitter_1_p8, splitter_1_p9, splitter_1_p10, splitter_1_p11, splitter_1_p12
  // Splitter splitter_13: pin names not known; wires that end beside it: splitter_2_p1, splitter_2_p2, splitter_2_p3, splitter_2_p4, splitter_1_p1, splitter_1_p2, splitter_1_p3, splitter_1_p4, splitter_1_p5, splitter_1_p6, splitter_1_p7, splitter_1_p8, splitter_1_p9, splitter_1_p10, splitter_1_p11, splitter_1_p12, splitter_13_p17
  RAM #(.addrWidth(12), .dataWidth(16), .bus("separate")) ram_1 (
    .addr(pin_6_p3), .din(splitter_13_p17), .data(ram_1_data), .str(pin_8_p5), .clk(pin_8_p5), .ld(undriven));  // open: sel, clr
  // Splitter splitter_14: pin names not known; wires that end beside it: ram_1_data, splitter_2_p1, splitter_2_p2, splitter_2_p3, splitter_2_p4, splitter_1_p1, splitter_1_p2, splitter_1_p3, splitter_1_p4, splitter_1_p5, splitter_1_p6, splitter_1_p7, splitter_1_p8, splitter_1_p9, splitter_1_p10, splitter_1_p11, splitter_1_p12
endmodule

module DR (
);

  wire pin_1_p1, pin_3_p1, pin_4_p1, pin_5_p1, pin_6_p1;
  wire [15:0] adder_1_out, constant_1_p1, controlled_buffer_1_out, controlled_buffer_2_out,
       controlled_buffer_4_out, pin_2_p1, register_1_q;

  // Pin pin_1: pin names not known; wires that end beside it: pin_1_p1
  // Pin pin_2: pin names not known; wires that end beside it: pin_2_p1
  // Pin pin_3: pin names not known; wires that end beside it: pin_3_p1
  // Constant constant_1: pin names not known; wires that end beside it: constant_1_p1
  Adder #(.width(16)) adder_1 (.a(controlled_buffer_2_out), .b(constant_1_p1), .out(adder_1_out));  // open: cin, cout
  assign controlled_buffer_1_out = pin_3_p1 ? pin_2_p1 : 16'bz;  // Controlled_Buffer controlled_buffer_1
  assign controlled_buffer_2_out = pin_1_p1 ? register_1_q : 16'bz;  // Controlled_Buffer controlled_buffer_2
  assign controlled_buffer_1_out = pin_1_p1 ? adder_1_out : 16'bz;  // Controlled_Buffer controlled_buffer_3
  // Pin pin_4: pin names not known; wires that end beside it: pin_4_p1
  // Pin pin_5: pin names not known; wires that end beside it: pin_5_p1
  Register #(.width(16), .trigger("falling")) register_1 (
    .D(controlled_buffer_1_out), .Q(register_1_q), .clk(pin_4_p1), .clr(pin_5_p1));  // open: en
  // Pin pin_6: pin names not known; wires that end beside it: pin_6_p1
  // Pin pin_7: pin names not known; wires that end beside it: register_1_q
  assign controlled_buffer_4_out = pin_6_p1 ? register_1_q : 16'bz;  // Controlled_Buffer controlled_buffer_4
  // Pin pin_8: pin names not known; wires that end beside it: controlled_buffer_4_out
endmodule

module CU (
);

  wire and_1_out, and_2_out, and_3_out, comparator_1_eq, comparator_2_eq, comparator_3_eq, comparator_4_eq,
       comparator_5_eq, comparator_6_eq, comparator_7_eq, comparator_8_eq, comparator_9_eq, comparator_10_eq,
       comparator_11_eq, comparator_12_eq, comparator_13_eq, constant_1_p1, constant_2_p1,
       demultiplexer_1_out0, demultiplexer_1_out1, demultiplexer_2_out0, demultiplexer_2_out1,
       demultiplexer_3_out0, demultiplexer_4_out0, demultiplexer_4_out1, demultiplexer_4_out2,
       demultiplexer_4_out3, demultiplexer_4_out4, demultiplexer_4_out5, demultiplexer_4_out6,
       demultiplexer_4_out7, demultiplexer_4_out8, demultiplexer_4_out9, demultiplexer_4_out10,
       demultiplexer_4_out11, demultiplexer_5_out1, demultiplexer_6_out1, demultiplexer_7_out1,
       demultiplexer_8_out1, demultiplexer_9_out0, demultiplexer_9_out1, demultiplexer_9_out2,
       demultiplexer_9_out3, demultiplexer_9_out4, demultiplexer_9_out5, demultiplexer_9_out6,
       demultiplexer_10_out0, demultiplexer_10_out1, demultiplexer_10_out2, demultiplexer_10_out3,
       demultiplexer_10_out4, demultiplexer_10_out5, demultiplexer_10_out6, demultiplexer_11_out0,
       demultiplexer_11_out1, not_1_out, not_2_out, not_3_out, not_4_out, not_5_out, not_6_out, not_7_out,
       not_8_out, not_9_out, not_10_out, not_11_out, not_12_out, not_13_out, not_14_out, not_15_out,
       not_16_out, not_17_out, not_18_out, not_19_out, not_20_out, not_21_out, not_22_out, not_23_out,
       not_24_out, not_25_out, or_1_out, or_2_out, or_3_out, or_4_out, or_5_out, or_6_out, or_7_out,
       or_8_out, or_9_out, or_10_out, or_11_out, or_12_out, or_13_out, pin_1_p1, pin_2_p1, pin_3_p1,
       pin_4_p1, pin_7_p1, pin_8_p1, pin_9_p1, pin_10_p1, pin_11_p1, pin_12_p1, pin_13_p1, pin_14_p1,
       pin_15_p1, pin_16_p1, pin_17_p1, pin_18_p1, pin_19_p1, pin_20_p1, pin_21_p1, pin_22_p1, pin_23_p1,
       pin_24_p1, pin_25_p1, pin_26_p1, pin_27_p1, pin_29_p1, pin_31_p1, splitter_1_p2, splitter_1_p4,
       splitter_2_p2;
  wire [2:0] constant_11_p1, constant_12_p1, constant_13_p1, splitter_1_p3;
  wire [3:0] pin_5_p3;
  wire [7:0] constant_3_p1, constant_4_p1, constant_5_p1, constant_6_p1, constant_7_p1, constant_8_p1,
       constant_9_p1, constant_10_p1, counter_1_q;
  wire [15:0] constant_14_p3, constant_15_p1, pin_28_p3, pin_32_p1;

  // Pin pin_1: pin names not known; wires that end beside it: pin_1_p1
  // Pin pin_2: pin names not known; wires that end beside it: pin_2_p1
  // Pin pin_3: pin names not known; wires that end beside it: pin_3_p1
  // Pin pin_4: pin names not known; wires that end beside it: pin_4_p1
  // Constant constant_1: pin names not known; wires that end beside it: constant_1_p1
  // Constant constant_2: pin names not known; wires that end beside it: constant_2_p1
  Counter #(.trigger("falling")) counter_1 (
    .Q(counter_1_q), .clk(pin_1_p1), .clr(or_1_out));  // open: load, D, count, carry
  // Constant constant_3: pin names not known; wires that end beside it: constant_3_p1
  // Constant constant_4: pin names not known; wires that end beside it: constant_4_p1
  // Constant constant_5: pin names not known; wires that end beside it: constant_5_p1
  // Constant constant_6: pin names not known; wires that end beside it: constant_6_p1
  // Constant constant_7: pin names not known; wires that end beside it: constant_7_p1
  // Constant constant_8: pin names not known; wires that end beside it: constant_8_p1
  // Constant constant_9: pin names not known; wires that end beside it: constant_9_p1
  // Constant constant_10: pin names not known; wires that end beside it: constant_10_p1
  or or_1 (or_1_out, demultiplexer_2_out1, demultiplexer_11_out0, comparator_8_eq, demultiplexer_10_out3, demultiplexer_10_out4);
  // Pin pin_5: pin names not known; wires that end beside it: pin_2_p1, pin_2_p1, pin_5_p3
  Comparator comparator_1 (.a(counter_1_q), .b(constant_3_p1), .eq(comparator_1_eq));  // open: gt, lt
  Comparator comparator_2 (.a(counter_1_q), .b(constant_4_p1), .eq(comparator_2_eq));  // open: gt, lt
  Comparator comparator_3 (.a(counter_1_q), .b(constant_5_p1), .eq(comparator_3_eq));  // open: gt, lt
  Comparator comparator_4 (.a(counter_1_q), .b(constant_6_p1), .eq(comparator_4_eq));  // open: gt, lt
  Comparator comparator_5 (.a(counter_1_q), .b(constant_7_p1), .eq(comparator_5_eq));  // open: gt, lt
  Comparator comparator_6 (.a(counter_1_q), .b(constant_8_p1), .eq(comparator_6_eq));  // open: gt, lt
  Comparator comparator_7 (.a(counter_1_q), .b(constant_9_p1), .eq(comparator_7_eq));  // open: gt, lt
  Comparator comparator_8 (.a(counter_1_q), .b(constant_10_p1), .eq(comparator_8_eq));  // open: gt, lt
  TABLE table_1 ();
  // Splitter splitter_1: pin names not known; wires that end beside it: pin_2_p1, splitter_1_p2, splitter_1_p3, splitter_1_p4
  Demultiplexer demultiplexer_1 (
    .out0(demultiplexer_1_out0), .out1(demultiplexer_1_out1), .in(comparator_4_eq), .sel(and_3_out));  // open: en
  Demultiplexer #(.disabled(0)) demultiplexer_2 (
    .out0(demultiplexer_2_out0), .out1(demultiplexer_2_out1), .in(comparator_5_eq), .sel(and_1_out));  // open: en
  Demultiplexer #(.disabled(0)) demultiplexer_3 (
    .out0(demultiplexer_3_out0), .in(comparator_6_eq), .sel(and_1_out));  // open: out1, en
  // Pin pin_6: pin names not known; wires that end beside it: splitter_1_p3
  // Pin pin_7: pin names not known; wires that end beside it: pin_7_p1
  assign pin_7_p1 = not_1_out ? constant_2_p1 : 1'bz;  // Controlled_Buffer controlled_buffer_1
  not not_1 (not_1_out, or_2_out);
  assign pin_7_p1 = or_2_out ? pin_3_p1 : 1'bz;  // Controlled_Buffer controlled_buffer_2
  // Constant constant_11: pin names not known; wires that end beside it: constant_11_p1, splitter_1_p2
  // Constant constant_12: pin names not known; wires that end beside it: constant_12_p1
  // Constant constant_13: pin names not known; wires that end beside it: constant_13_p1
  or or_2 (or_2_out, demultiplexer_9_out4, demultiplexer_10_out5);
  Comparator #(.width(3)) comparator_9 (.a(splitter_1_p3), .b(constant_11_p1), .eq(comparator_9_eq));  // open: gt, lt
  not not_2 (not_2_out, splitter_1_p4);
  Comparator #(.width(3)) comparator_10 (.a(splitter_1_p3), .b(constant_12_p1), .eq(comparator_10_eq));  // open: gt, lt
  Comparator #(.width(3)) comparator_11 (.a(splitter_1_p3), .b(constant_13_p1), .eq(comparator_11_eq));  // open: gt, lt
  // Pin pin_8: pin names not known; wires that end beside it: pin_8_p1
  assign pin_8_p1 = not_3_out ? constant_2_p1 : 1'bz;  // Controlled_Buffer controlled_buffer_3
  not not_3 (not_3_out, or_3_out);
  assign pin_8_p1 = or_3_out ? pin_4_p1 : 1'bz;  // Controlled_Buffer controlled_buffer_4
  not not_4 (not_4_out, comparator_11_eq);
  or or_3 (or_3_out, comparator_1_eq, demultiplexer_9_out5);
  and and_1 (and_1_out, comparator_9_eq, not_2_out);
  and and_2 (and_2_out, comparator_10_eq, splitter_1_p4);
  and and_3 (and_3_out, not_4_out, splitter_1_p4);
  // Pin pin_9: pin names not known; wires that end beside it: pin_9_p1
  assign pin_9_p1 = not_5_out ? constant_2_p1 : 1'bz;  // Controlled_Buffer controlled_buffer_5
  not not_5 (not_5_out, or_4_out);
  assign pin_9_p1 = or_4_out ? pin_4_p1 : 1'bz;  // Controlled_Buffer controlled_buffer_6
  or or_4 (or_4_out, comparator_2_eq, demultiplexer_1_out1, demultiplexer_9_out0, demultiplexer_9_out1, demultiplexer_9_out2, demultiplexer_9_out6);
  // Pin pin_10: pin names not known; wires that end beside it: pin_10_p1
  assign pin_10_p1 = not_6_out ? constant_2_p1 : 1'bz;  // Controlled_Buffer controlled_buffer_7
  or or_5 (or_5_out, and_1_out, and_3_out, and_2_out);
  not not_6 (not_6_out, or_6_out);
  assign pin_10_p1 = or_6_out ? pin_3_p1 : 1'bz;  // Controlled_Buffer controlled_buffer_8
  or or_6 (or_6_out, demultiplexer_9_out3, demultiplexer_9_out5, comparator_7_eq);
  not not_7 (not_7_out, or_5_out);
  // Pin pin_11: pin names not known; wires that end beside it: pin_11_p1
  assign pin_11_p1 = not_8_out ? constant_2_p1 : 1'bz;  // Controlled_Buffer controlled_buffer_9
  not not_8 (not_8_out, or_7_out);
  assign pin_11_p1 = or_7_out ? pin_3_p1 : 1'bz;  // Controlled_Buffer controlled_buffer_10
  or or_7 (or_7_out, comparator_1_eq, comparator_3_eq, demultiplexer_1_out1);
  // Pin pin_12: pin names not known; wires that end beside it: pin_12_p1
  assign pin_12_p1 = not_9_out ? constant_2_p1 : 1'bz;  // Controlled_Buffer controlled_buffer_11
  not not_9 (not_9_out, or_8_out);
  assign pin_12_p1 = or_8_out ? pin_4_p1 : 1'bz;  // Controlled_Buffer controlled_buffer_12
  or or_8 (or_8_out, demultiplexer_9_out4, demultiplexer_10_out5);
  // Pin pin_13: pin names not known; wires that end beside it: pin_13_p1
  assign pin_13_p1 = not_10_out ? constant_2_p1 : 1'bz;  // Controlled_Buffer controlled_buffer_13
  not not_10 (not_10_out, comparator_2_eq);
  assign pin_13_p1 = comparator_2_eq ? pin_3_p1 : 1'bz;  // Controlled_Buffer controlled_buffer_14
  // Pin pin_14: pin names not known; wires that end beside it: pin_14_p1
  assign pin_14_p1 = not_11_out ? constant_2_p1 : 1'bz;  // Controlled_Buffer controlled_buffer_15
  not not_11 (not_11_out, comparator_3_eq);
  assign pin_14_p1 = comparator_3_eq ? pin_4_p1 : 1'bz;  // Controlled_Buffer controlled_buffer_16
  // Pin pin_15: pin names not known; wires that end beside it: pin_15_p1
  assign pin_15_p1 = not_12_out ? constant_2_p1 : 1'bz;  // Controlled_Buffer controlled_buffer_17
  not not_12 (not_12_out, demultiplexer_9_out3);
  assign pin_15_p1 = demultiplexer_9_out3 ? pin_4_p1 : 1'bz;  // Controlled_Buffer controlled_buffer_18
  // Pin pin_16: pin names not known; wires that end beside it: pin_16_p1
  assign pin_16_p1 = not_13_out ? constant_2_p1 : 1'bz;  // Controlled_Buffer controlled_buffer_19
  not not_13 (not_13_out, demultiplexer_10_out2);
  assign pin_16_p1 = demultiplexer_10_out2 ? pin_3_p1 : 1'bz;  // Controlled_Buffer controlled_buffer_20
  // Pin pin_17: pin names not known; wires that end beside it: pin_17_p1
  assign pin_17_p1 = not_14_out ? constant_2_p1 : 1'bz;  // Controlled_Buffer controlled_buffer_21
  not not_14 (not_14_out, or_9_out);
  assign pin_17_p1 = or_9_out ? pin_3_p1 : 1'bz;  // Controlled_Buffer controlled_buffer_22
  or or_9 (or_9_out, demultiplexer_9_out0, demultiplexer_9_out1, demultiplexer_9_out2, demultiplexer_9_out6);
  // Pin pin_18: pin names not known; wires that end beside it: pin_18_p1
  assign pin_18_p1 = not_15_out ? constant_2_p1 : 1'bz;  // Controlled_Buffer controlled_buffer_23
  not not_15 (not_15_out, or_10_out);
  assign pin_18_p1 = or_10_out ? pin_4_p1 : 1'bz;  // Controlled_Buffer controlled_buffer_24
  or or_10 (or_10_out, demultiplexer_10_out2, comparator_7_eq);
  // Pin pin_19: pin names not known; wires that end beside it: pin_19_p1
  assign pin_19_p1 = not_16_out ? constant_2_p1 : 1'bz;  // Controlled_Buffer controlled_buffer_25
  assign pin_19_p1 = or_11_out ? pin_3_p1 : 1'bz;  // Controlled_Buffer controlled_buffer_26
  not not_16 (not_16_out, or_11_out);
  or or_11 (or_11_out, demultiplexer_10_out0, demultiplexer_10_out1);
  // Pin pin_20: pin names not known; wires that end beside it: pin_20_p1
  assign pin_20_p1 = not_17_out ? constant_2_p1 : 1'bz;  // Controlled_Buffer controlled_buffer_27
  not not_17 (not_17_out, or_12_out);
  assign pin_20_p1 = or_12_out ? pin_3_p1 : 1'bz;  // Controlled_Buffer controlled_buffer_28
  or or_12 (or_12_out, comparator_2_eq, demultiplexer_11_out1, demultiplexer_6_out1, demultiplexer_7_out1, demultiplexer_8_out1);
  // Pin pin_21: pin names not known; wires that end beside it: pin_21_p1
  assign pin_21_p1 = not_18_out ? constant_2_p1 : 1'bz;  // Controlled_Buffer controlled_buffer_29
  not not_18 (not_18_out, demultiplexer_1_out1);
  assign pin_21_p1 = demultiplexer_1_out1 ? pin_3_p1 : 1'bz;  // Controlled_Buffer controlled_buffer_30
  // Pin pin_22: pin names not known; wires that end beside it: pin_22_p1
  assign pin_22_p1 = not_19_out ? constant_2_p1 : 1'bz;  // Controlled_Buffer controlled_buffer_31
  not not_19 (not_19_out, demultiplexer_9_out5);
  assign pin_22_p1 = demultiplexer_9_out5 ? pin_3_p1 : 1'bz;  // Controlled_Buffer controlled_buffer_32
  // Pin pin_23: pin names not known; wires that end beside it: pin_23_p1
  assign pin_23_p1 = not_20_out ? constant_2_p1 : 1'bz;  // Controlled_Buffer controlled_buffer_33
  assign pin_23_p1 = demultiplexer_10_out6 ? pin_3_p1 : 1'bz;  // Controlled_Buffer controlled_buffer_34
  not not_20 (not_20_out, demultiplexer_10_out6);
  // Pin pin_24: pin names not known; wires that end beside it: pin_24_p1
  assign pin_24_p1 = not_21_out ? constant_2_p1 : 1'bz;  // Controlled_Buffer controlled_buffer_35
  not not_21 (not_21_out, demultiplexer_4_out0);
  assign pin_24_p1 = demultiplexer_4_out0 ? pin_3_p1 : 1'bz;  // Controlled_Buffer controlled_buffer_36
  // Pin pin_25: pin names not known; wires that end beside it: pin_25_p1
  assign pin_25_p1 = not_22_out ? constant_2_p1 : 1'bz;  // Controlled_Buffer controlled_buffer_37
  not not_22 (not_22_out, demultiplexer_4_out1);
  assign pin_25_p1 = demultiplexer_4_out1 ? pin_3_p1 : 1'bz;  // Controlled_Buffer controlled_buffer_38
  // Pin pin_26: pin names not known; wires that end beside it: pin_26_p1
  assign pin_26_p1 = not_23_out ? constant_2_p1 : 1'bz;  // Controlled_Buffer controlled_buffer_39
  not not_23 (not_23_out, or_13_out);
  assign pin_26_p1 = or_13_out ? pin_3_p1 : 1'bz;  // Controlled_Buffer controlled_buffer_40
  or or_13 (or_13_out, demultiplexer_4_out2, demultiplexer_4_out3, demultiplexer_4_out4, demultiplexer_4_out5, demultiplexer_4_out6);
  // Pin pin_27: pin names not known; wires that end beside it: pin_27_p1
  and and_4 (pin_27_p1, constant_2_p1, pin_3_p1);
  // Pin pin_28: pin names not known; wires that end beside it: comparator_2_eq, comparator_3_eq, pin_28_p3
  // Pin pin_29: pin names not known; wires that end beside it: pin_29_p1, pin_3_p1, pin_4_p1
  and and_5 (pin_29_p1, constant_2_p1, pin_3_p1);
  Demultiplexer #(.select(4), .disabled(0)) demultiplexer_4 (
    .out0(demultiplexer_4_out0), .out1(demultiplexer_4_out1), .out2(demultiplexer_4_out2),
    .out3(demultiplexer_4_out3), .out4(demultiplexer_4_out4), .out5(demultiplexer_4_out5),
    .out6(demultiplexer_4_out6), .out7(demultiplexer_4_out7), .out8(demultiplexer_4_out8),
    .out9(demultiplexer_4_out9), .out10(demultiplexer_4_out10), .out11(demultiplexer_4_out11),
    .in(demultiplexer_1_out0), .sel(pin_5_p3), .en(and_1_out));  // open: out12, out13, out14, out15
  // Pin pin_30: pin names not known; wires that end beside it: demultiplexer_4_out11, demultiplexer_4_out0, demultiplexer_4_out1, demultiplexer_4_out2, demultiplexer_4_out3, demultiplexer_4_out4, demultiplexer_4_out5, demultiplexer_4_out6
  // Splitter splitter_2: pin names not known; wires that end beside it: pin_28_p3, splitter_2_p2
  // Pin pin_31: pin names not known; wires that end beside it: pin_31_p1
  // Constant constant_14: pin names not known; wires that end beside it: demultiplexer_1_out1, demultiplexer_2_out1, constant_14_p3
  Comparator #(.width(16)) comparator_12 (.a(pin_28_p3), .b(constant_14_p3), .eq(comparator_12_eq));  // open: gt, lt
  Demultiplexer #(.disabled(0)) demultiplexer_5 (
    .out1(demultiplexer_5_out1), .in(demultiplexer_4_out10), .sel(not_25_out), .en(and_1_out));  // open: out0
  not not_24 (not_24_out, splitter_2_p2);
  not not_25 (not_25_out, pin_31_p1);
  Demultiplexer #(.disabled(0)) demultiplexer_6 (
    .out1(demultiplexer_6_out1), .in(demultiplexer_4_out7), .sel(not_24_out), .en(and_1_out));  // open: out0
  Demultiplexer #(.disabled(0)) demultiplexer_7 (
    .out1(demultiplexer_7_out1), .in(demultiplexer_4_out8), .sel(splitter_2_p2), .en(and_1_out));  // open: out0
  Demultiplexer #(.disabled(0)) demultiplexer_8 (
    .out1(demultiplexer_8_out1), .in(demultiplexer_4_out9), .sel(comparator_12_eq), .en(and_1_out));  // open: out0
  Demultiplexer #(.select(3), .disabled(0)) demultiplexer_9 (
    .out0(demultiplexer_9_out0), .out1(demultiplexer_9_out1), .out2(demultiplexer_9_out2),
    .out3(demultiplexer_9_out3), .out4(demultiplexer_9_out4), .out5(demultiplexer_9_out5),
    .out6(demultiplexer_9_out6), .in(demultiplexer_2_out0), .sel(splitter_1_p3), .en(not_7_out));  // open: out7
  Demultiplexer #(.select(3), .disabled(0)) demultiplexer_10 (
    .out0(demultiplexer_10_out0), .out1(demultiplexer_10_out1), .out2(demultiplexer_10_out2),
    .out3(demultiplexer_10_out3), .out4(demultiplexer_10_out4), .out5(demultiplexer_10_out5),
    .out6(demultiplexer_10_out6), .in(demultiplexer_3_out0), .sel(splitter_1_p3), .en(not_7_out));  // open: out7
  // Pin pin_32: pin names not known; wires that end beside it: pin_32_p1
  // Constant constant_15: pin names not known; wires that end beside it: constant_15_p1, demultiplexer_10_out0, demultiplexer_10_out1, demultiplexer_10_out2, demultiplexer_10_out3, demultiplexer_10_out4, demultiplexer_10_out5, demultiplexer_10_out6
  Comparator #(.width(16)) comparator_13 (.a(pin_32_p1), .b(constant_15_p1), .eq(comparator_13_eq));  // open: gt, lt
  Demultiplexer #(.disabled(0)) demultiplexer_11 (
    .out0(demultiplexer_11_out0), .out1(demultiplexer_11_out1), .in(comparator_7_eq), .sel(comparator_13_eq),
    .en(not_7_out));

  // Notes on the sheet:
  //   S
  //   E
  //   PCS
  //   PCE
  //   ME
  //   MS
  //   ARS
  //   ARE
  //   IRS
  //   IRE
  //   ACE
  //   ACS
  //   DRS
  //   DRE
  //   LDAFALU1
  //   PC++
  //   DEC
  //   AR++
  //   DR++
  //   CLA
  //   CLE
  //   LDAFALU2C
  //   TMPS
  //   TMPE
endmodule

module CLOCK (
);

  wire constant_1_p1, j_k_ff_1_q, j_k_ff_1_qn, nand_1_out, nand_2_out, not_1_out, pin_1_p1;

  // Pin pin_1: pin names not known; wires that end beside it: pin_1_p1
  // Constant constant_1: pin names not known; wires that end beside it: constant_1_p1
  J_K_Flip_Flop j_k_ff_1 (
    .J(constant_1_p1), .clk(pin_1_p1), .K(constant_1_p1), .Q(j_k_ff_1_q), .Qn(j_k_ff_1_qn));  // open: preset, en, reset
  nand nand_1 (nand_1_out, pin_1_p1, j_k_ff_1_q);
  nand nand_2 (nand_2_out, j_k_ff_1_qn, pin_1_p1);
  not not_1 (not_1_out, nand_1_out);
  // Pin pin_2: pin names not known; wires that end beside it: j_k_ff_1_q
  // Pin pin_3: pin names not known; wires that end beside it: not_1_out
  // Pin pin_4: pin names not known; wires that end beside it: nand_2_out
endmodule

module ALU1 (
);

  wire adder_1_cout, and_1_out, and_2_out, and_3_out, and_4_out, and_5_out, and_7_out, comparator_1_eq,
       comparator_2_eq, comparator_3_eq, comparator_4_eq, comparator_5_eq, comparator_6_eq, not_2_out,
       pin_1_p1, pin_4_p1, pin_9_p1, splitter_1_p2, splitter_2_p3;
  wire [2:0] constant_9_p1, pin_3_p1;
  wire [4:0] constant_1_p1, constant_7_p1;
  wire [15:0] adder_1_out, adder_2_out, and_6_out, constant_2_p1, constant_3_p1, constant_4_p1,
       constant_5_p1, constant_6_p1, constant_8_p1, multiplexer_1_out, not_1_out, pin_2_p1, pin_4_p2,
       splitter_1_p1, splitter_2_p2;
  wire [16:0] controlled_buffer_1_out, shifter_1_out, shifter_2_out, splitter_1_p3, splitter_3_p1;

  // Pin pin_1: pin names not known; wires that end beside it: pin_1_p1
  // Pin pin_2: pin names not known; wires that end beside it: pin_2_p1
  // Splitter splitter_1: pin names not known; wires that end beside it: splitter_1_p1, splitter_1_p2, splitter_1_p3
  // Constant constant_1: pin names not known; wires that end beside it: constant_1_p1
  // Constant constant_2: pin names not known; wires that end beside it: constant_2_p1
  // Constant constant_3: pin names not known; wires that end beside it: constant_3_p1
  // Constant constant_4: pin names not known; wires that end beside it: constant_4_p1
  // Constant constant_5: pin names not known; wires that end beside it: constant_5_p1
  // Constant constant_6: pin names not known; wires that end beside it: constant_6_p1, pin_1_p1
  Shifter #(.width(17), .shift("rr")) shifter_1 (.in(splitter_1_p3), .\dist (constant_1_p1), .out(shifter_1_out));
  // Constant constant_7: pin names not known; wires that end beside it: constant_7_p1
  Comparator #(.width(16)) comparator_1 (.a(pin_2_p1), .b(constant_2_p1), .eq(comparator_1_eq));  // open: gt, lt
  Comparator #(.width(16)) comparator_2 (.a(pin_2_p1), .b(constant_3_p1), .eq(comparator_2_eq));  // open: gt, lt
  Comparator #(.width(16)) comparator_3 (.a(pin_2_p1), .b(constant_4_p1), .eq(comparator_3_eq));  // open: gt, lt
  Comparator #(.width(16)) comparator_4 (.a(pin_2_p1), .b(constant_5_p1), .eq(comparator_4_eq));  // open: gt, lt
  Comparator #(.width(16)) comparator_5 (.a(pin_2_p1), .b(constant_6_p1), .eq(comparator_5_eq));  // open: gt, lt
  // Pin pin_3: pin names not known; wires that end beside it: pin_3_p1
  // Pin pin_4: pin names not known; wires that end beside it: pin_4_p1, pin_4_p2
  assign controlled_buffer_1_out = and_1_out ? shifter_1_out : 17'bz;  // Controlled_Buffer controlled_buffer_1
  Shifter #(.width(17), .shift("rl")) shifter_2 (.in(splitter_1_p3), .\dist (constant_7_p1), .out(shifter_2_out));
  and and_1 (and_1_out, pin_1_p1, comparator_3_eq);
  // Pin pin_5: pin names not known; wires that end beside it: pin_4_p2
  // Splitter splitter_2: pin names not known; wires that end beside it: controlled_buffer_1_out, splitter_2_p2, splitter_2_p3
  // Splitter splitter_3: pin names not known; wires that end beside it: splitter_3_p1, splitter_2_p2, splitter_2_p3
  assign splitter_3_p1 = and_2_out ? shifter_2_out : 17'bz;  // Controlled_Buffer controlled_buffer_2
  and and_2 (and_2_out, pin_1_p1, comparator_4_eq);
  // Pin pin_6: pin names not known; wires that end beside it: splitter_1_p1
  // Pin pin_7: pin names not known; wires that end beside it: splitter_2_p2
  and and_3 (and_3_out, comparator_1_eq, pin_1_p1);
  and and_4 (and_4_out, comparator_2_eq, pin_1_p1);
  and and_5 (and_5_out, comparator_5_eq, pin_1_p1);
  // Constant constant_8: pin names not known; wires that end beside it: constant_8_p1
  Adder #(.width(16)) adder_1 (.a(pin_4_p2), .b(splitter_1_p1), .out(adder_1_out), .cout(adder_1_cout));  // open: cin
  assign splitter_2_p3 = and_7_out ? adder_1_cout : 1'bz;  // Controlled_Buffer controlled_buffer_3
  Adder #(.width(16)) adder_2 (.a(splitter_1_p1), .b(constant_8_p1), .out(adder_2_out));  // open: cin, cout
  assign and_6_out = pin_4_p2 & splitter_1_p1;  // AND_Gate and_6, 16 bits wide
  // Constant constant_9: pin names not known; wires that end beside it: constant_9_p1
  assign not_1_out = ~splitter_1_p1;  // NOT_Gate not_1, 16 bits wide
  assign splitter_2_p2 = and_5_out ? adder_2_out : 16'bz;  // Controlled_Buffer controlled_buffer_4
  Comparator #(.width(3)) comparator_6 (.a(pin_3_p1), .b(constant_9_p1), .eq(comparator_6_eq));  // open: gt, lt
  and and_7 (and_7_out, comparator_6_eq, pin_4_p1);
  assign splitter_2_p2 = and_3_out ? not_1_out : 16'bz;  // Controlled_Buffer controlled_buffer_5
  not not_2 (not_2_out, splitter_1_p2);
  assign splitter_2_p3 = and_4_out ? not_2_out : 1'bz;  // Controlled_Buffer controlled_buffer_6
  Multiplexer #(.select(3), .width(16)) multiplexer_1 (
    .in0(and_6_out), .in1(adder_1_out), .in2(pin_4_p2), .in3(splitter_1_p1), .out(multiplexer_1_out),
    .sel(pin_3_p1));  // open: in4, in5, in6, in7, en
  assign splitter_2_p2 = pin_4_p1 ? multiplexer_1_out : 16'bz;  // Controlled_Buffer controlled_buffer_7
  // Pin pin_8: pin names not known; wires that end beside it: splitter_2_p2
  // Pin pin_9: pin names not known; wires that end beside it: pin_9_p1
  // Pin pin_10: pin names not known; wires that end beside it: splitter_1_p2
  Register #(.width(1), .trigger("falling")) register_1 (
    .D(splitter_2_p3), .Q(splitter_1_p2), .clk(pin_1_p1), .clr(pin_9_p1));  // open: en

  // Notes on the sheet:
  //   AC+E
  //   DR
  //   AC
endmodule

module TABLE (
);

  wire comparator_1_eq, comparator_2_eq, comparator_3_eq, comparator_4_eq, comparator_5_eq, comparator_6_eq,
       comparator_7_eq, comparator_8_eq, comparator_9_eq, comparator_10_eq, comparator_11_eq,
       comparator_12_eq, not_1_out;
  wire [3:0] adder_1_out, adder_2_out, adder_3_out, adder_4_out, adder_5_out, adder_6_out, adder_7_out,
       adder_8_out, adder_9_out, adder_10_out, bit_extender_1_p2, bit_extender_2_p2, bit_extender_3_p2,
       bit_extender_4_p2, bit_extender_5_p2, bit_extender_6_p2, bit_extender_7_p2, bit_extender_8_p2,
       bit_extender_9_p2, bit_extender_10_p2, bit_extender_11_p2, bit_extender_12_p2, constant_13_p1,
       constant_14_p1, constant_15_p1, constant_16_p1, constant_17_p1, constant_18_p1, constant_19_p1,
       constant_20_p1, constant_21_p1, constant_22_p1, controlled_buffer_1_out;
  wire [15:0] constant_1_p1, constant_2_p1, constant_3_p1, constant_4_p1, constant_5_p1, constant_6_p1,
       constant_7_p1, constant_8_p1, constant_9_p1, constant_10_p1, constant_11_p1, constant_12_p1, pin_1_p1;

  // Pin pin_1: pin names not known; wires that end beside it: pin_1_p1
  // Constant constant_1: pin names not known; wires that end beside it: constant_1_p1
  // Constant constant_2: pin names not known; wires that end beside it: constant_2_p1
  // Constant constant_3: pin names not known; wires that end beside it: constant_3_p1
  // Constant constant_4: pin names not known; wires that end beside it: constant_4_p1
  // Constant constant_5: pin names not known; wires that end beside it: constant_5_p1
  // Constant constant_6: pin names not known; wires that end beside it: constant_6_p1
  // Constant constant_7: pin names not known; wires that end beside it: constant_7_p1
  // Constant constant_8: pin names not known; wires that end beside it: constant_8_p1
  // Constant constant_9: pin names not known; wires that end beside it: constant_9_p1
  // Constant constant_10: pin names not known; wires that end beside it: constant_10_p1
  // Constant constant_11: pin names not known; wires that end beside it: constant_11_p1
  // Constant constant_12: pin names not known; wires that end beside it: constant_12_p1
  Comparator #(.width(16)) comparator_1 (.a(pin_1_p1), .b(constant_1_p1), .eq(comparator_1_eq));  // open: gt, lt
  Comparator #(.width(16)) comparator_2 (.a(pin_1_p1), .b(constant_2_p1), .eq(comparator_2_eq));  // open: gt, lt
  Comparator #(.width(16)) comparator_3 (.a(pin_1_p1), .b(constant_3_p1), .eq(comparator_3_eq));  // open: gt, lt
  Comparator #(.width(16)) comparator_4 (.a(pin_1_p1), .b(constant_4_p1), .eq(comparator_4_eq));  // open: gt, lt
  Comparator #(.width(16)) comparator_5 (.a(pin_1_p1), .b(constant_5_p1), .eq(comparator_5_eq));  // open: gt, lt
  Comparator #(.width(16)) comparator_6 (.a(pin_1_p1), .b(constant_6_p1), .eq(comparator_6_eq));  // open: gt, lt
  Comparator #(.width(16)) comparator_7 (.a(pin_1_p1), .b(constant_7_p1), .eq(comparator_7_eq));  // open: gt, lt
  Comparator #(.width(16)) comparator_8 (.a(pin_1_p1), .b(constant_8_p1), .eq(comparator_8_eq));  // open: gt, lt
  Comparator #(.width(16)) comparator_9 (.a(pin_1_p1), .b(constant_9_p1), .eq(comparator_9_eq));  // open: gt, lt
  Comparator #(.width(16)) comparator_10 (.a(pin_1_p1), .b(constant_10_p1), .eq(comparator_10_eq));  // open: gt, lt
  Comparator #(.width(16)) comparator_11 (.a(pin_1_p1), .b(constant_11_p1), .eq(comparator_11_eq));  // open: gt, lt
  Comparator #(.width(16)) comparator_12 (.a(pin_1_p1), .b(constant_12_p1), .eq(comparator_12_eq));  // open: gt, lt
  not not_1 (not_1_out, comparator_1_eq);
  // Bit_Extender bit_extender_1: pin names not known; wires that end beside it: not_1_out, bit_extender_1_p2
  // Bit_Extender bit_extender_2: pin names not known; wires that end beside it: comparator_2_eq, bit_extender_2_p2
  // Bit_Extender bit_extender_3: pin names not known; wires that end beside it: comparator_3_eq, bit_extender_3_p2
  // Bit_Extender bit_extender_4: pin names not known; wires that end beside it: comparator_4_eq, bit_extender_4_p2
  // Bit_Extender bit_extender_5: pin names not known; wires that end beside it: comparator_5_eq, bit_extender_5_p2
  // Bit_Extender bit_extender_6: pin names not known; wires that end beside it: comparator_6_eq, bit_extender_6_p2
  // Bit_Extender bit_extender_7: pin names not known; wires that end beside it: comparator_7_eq, bit_extender_7_p2
  // Bit_Extender bit_extender_8: pin names not known; wires that end beside it: comparator_8_eq, bit_extender_8_p2
  // Bit_Extender bit_extender_9: pin names not known; wires that end beside it: comparator_9_eq, bit_extender_9_p2
  // Bit_Extender bit_extender_10: pin names not known; wires that end beside it: comparator_10_eq, bit_extender_10_p2
  // Bit_Extender bit_extender_11: pin names not known; wires that end beside it: comparator_11_eq, bit_extender_11_p2
  // Bit_Extender bit_extender_12: pin names not known; wires that end beside it: comparator_12_eq, bit_extender_12_p2
  assign controlled_buffer_1_out = comparator_1_eq ? bit_extender_1_p2 : 4'bz;  // Controlled_Buffer controlled_buffer_1
  assign controlled_buffer_1_out = comparator_2_eq ? bit_extender_2_p2 : 4'bz;  // Controlled_Buffer controlled_buffer_2
  // Constant constant_13: pin names not known; wires that end beside it: constant_13_p1
  // Constant constant_14: pin names not known; wires that end beside it: constant_14_p1
  // Constant constant_15: pin names not known; wires that end beside it: constant_15_p1
  // Constant constant_16: pin names not known; wires that end beside it: constant_16_p1
  // Constant constant_17: pin names not known; wires that end beside it: constant_17_p1
  // Constant constant_18: pin names not known; wires that end beside it: constant_18_p1
  // Constant constant_19: pin names not known; wires that end beside it: constant_19_p1
  // Constant constant_20: pin names not known; wires that end beside it: constant_20_p1
  // Constant constant_21: pin names not known; wires that end beside it: constant_21_p1
  // Constant constant_22: pin names not known; wires that end beside it: constant_22_p1
  Adder #(.width(4)) adder_1 (.a(bit_extender_3_p2), .b(constant_13_p1), .out(adder_1_out));  // open: cin, cout
  Adder #(.width(4)) adder_2 (.a(bit_extender_4_p2), .b(constant_14_p1), .out(adder_2_out));  // open: cin, cout
  Adder #(.width(4)) adder_3 (.a(bit_extender_5_p2), .b(constant_15_p1), .out(adder_3_out));  // open: cin, cout
  Adder #(.width(4)) adder_4 (.a(bit_extender_6_p2), .b(constant_16_p1), .out(adder_4_out));  // open: cin, cout
  Adder #(.width(4)) adder_5 (.a(bit_extender_7_p2), .b(constant_17_p1), .out(adder_5_out));  // open: cin, cout
  Adder #(.width(4)) adder_6 (.a(bit_extender_8_p2), .b(constant_18_p1), .out(adder_6_out));  // open: cin, cout
  Adder #(.width(4)) adder_7 (.a(bit_extender_9_p2), .b(constant_19_p1), .out(adder_7_out));  // open: cin, cout
  Adder #(.width(4)) adder_8 (.a(bit_extender_10_p2), .b(constant_20_p1), .out(adder_8_out));  // open: cin, cout
  Adder #(.width(4)) adder_9 (.a(bit_extender_11_p2), .b(constant_21_p1), .out(adder_9_out));  // open: cin, cout
  Adder #(.width(4)) adder_10 (.a(bit_extender_12_p2), .b(constant_22_p1), .out(adder_10_out));  // open: cin, cout
  assign controlled_buffer_1_out = comparator_3_eq ? adder_1_out : 4'bz;  // Controlled_Buffer controlled_buffer_3
  assign controlled_buffer_1_out = comparator_4_eq ? adder_2_out : 4'bz;  // Controlled_Buffer controlled_buffer_4
  assign controlled_buffer_1_out = comparator_5_eq ? adder_3_out : 4'bz;  // Controlled_Buffer controlled_buffer_5
  assign controlled_buffer_1_out = comparator_6_eq ? adder_4_out : 4'bz;  // Controlled_Buffer controlled_buffer_6
  assign controlled_buffer_1_out = comparator_7_eq ? adder_5_out : 4'bz;  // Controlled_Buffer controlled_buffer_7
  assign controlled_buffer_1_out = comparator_8_eq ? adder_6_out : 4'bz;  // Controlled_Buffer controlled_buffer_8
  assign controlled_buffer_1_out = comparator_9_eq ? adder_7_out : 4'bz;  // Controlled_Buffer controlled_buffer_9
  assign controlled_buffer_1_out = comparator_10_eq ? adder_8_out : 4'bz;  // Controlled_Buffer controlled_buffer_10
  assign controlled_buffer_1_out = comparator_11_eq ? adder_9_out : 4'bz;  // Controlled_Buffer controlled_buffer_11
  assign controlled_buffer_1_out = comparator_12_eq ? adder_10_out : 4'bz;  // Controlled_Buffer controlled_buffer_12
  // Pin pin_2: pin names not known; wires that end beside it: controlled_buffer_1_out
endmodule

module PC (
);

  wire pin_1_p1, pin_3_p1, pin_4_p1, pin_5_p1, pin_6_p1;
  wire [11:0] adder_1_out, constant_1_p1, controlled_buffer_1_out, controlled_buffer_2_out,
       controlled_buffer_4_out, pin_2_p1, register_1_q;

  // Pin pin_1: pin names not known; wires that end beside it: pin_1_p1
  // Constant constant_1: pin names not known; wires that end beside it: constant_1_p1
  // Pin pin_2: pin names not known; wires that end beside it: pin_2_p1
  assign controlled_buffer_1_out = pin_3_p1 ? register_1_q : 12'bz;  // Controlled_Buffer controlled_buffer_1
  Adder #(.width(12)) adder_1 (.a(controlled_buffer_1_out), .b(constant_1_p1), .out(adder_1_out));  // open: cin, cout
  // Pin pin_3: pin names not known; wires that end beside it: pin_3_p1
  assign controlled_buffer_2_out = pin_1_p1 ? pin_2_p1 : 12'bz;  // Controlled_Buffer controlled_buffer_2
  assign controlled_buffer_2_out = pin_3_p1 ? adder_1_out : 12'bz;  // Controlled_Buffer controlled_buffer_3
  // Pin pin_4: pin names not known; wires that end beside it: pin_4_p1
  // Pin pin_5: pin names not known; wires that end beside it: pin_5_p1
  Register #(.width(12), .trigger("falling")) register_1 (
    .D(controlled_buffer_2_out), .Q(register_1_q), .clk(pin_4_p1), .clr(pin_5_p1));  // open: en
  assign controlled_buffer_4_out = pin_6_p1 ? register_1_q : 12'bz;  // Controlled_Buffer controlled_buffer_4
  // Pin pin_6: pin names not known; wires that end beside it: pin_6_p1
  // Pin pin_7: pin names not known; wires that end beside it: register_1_q
  // Pin pin_8: pin names not known; wires that end beside it: controlled_buffer_4_out
endmodule

module IR (
);

  wire pin_1_p1, pin_3_p1, pin_4_p1, pin_5_p1, pin_6_p1;
  wire [15:0] constant_1_p1, controlled_buffer_1_out, controlled_buffer_2_out, controlled_buffer_4_out,
       pin_2_p1, register_1_q, subtractor_1_out;

  // Pin pin_1: pin names not known; wires that end beside it: pin_1_p1
  // Constant constant_1: pin names not known; wires that end beside it: constant_1_p1
  // Pin pin_2: pin names not known; wires that end beside it: pin_2_p1
  // Pin pin_3: pin names not known; wires that end beside it: pin_3_p1
  Subtractor #(.width(16)) subtractor_1 (
    .a(controlled_buffer_2_out), .b(constant_1_p1), .out(subtractor_1_out));  // open: bin, bout
  assign controlled_buffer_1_out = pin_1_p1 ? pin_2_p1 : 16'bz;  // Controlled_Buffer controlled_buffer_1
  assign controlled_buffer_2_out = pin_3_p1 ? register_1_q : 16'bz;  // Controlled_Buffer controlled_buffer_2
  assign controlled_buffer_1_out = pin_3_p1 ? subtractor_1_out : 16'bz;  // Controlled_Buffer controlled_buffer_3
  // Pin pin_4: pin names not known; wires that end beside it: pin_4_p1
  // Pin pin_5: pin names not known; wires that end beside it: pin_5_p1
  Register #(.width(16), .trigger("falling")) register_1 (
    .D(controlled_buffer_1_out), .Q(register_1_q), .clk(pin_4_p1), .clr(pin_5_p1));  // open: en
  // Pin pin_6: pin names not known; wires that end beside it: pin_6_p1
  // Pin pin_7: pin names not known; wires that end beside it: register_1_q
  assign controlled_buffer_4_out = pin_6_p1 ? register_1_q : 16'bz;  // Controlled_Buffer controlled_buffer_4
  // Pin pin_8: pin names not known; wires that end beside it: controlled_buffer_4_out
endmodule

module AR (
);

  wire pin_1_p1, pin_3_p1, pin_4_p1, pin_6_p1, pin_7_p1;
  wire [11:0] adder_1_out, constant_1_p1, controlled_buffer_1_out, controlled_buffer_3_out,
       controlled_buffer_4_out, pin_2_p1, register_1_q;

  // Constant constant_1: pin names not known; wires that end beside it: constant_1_p1
  Adder #(.width(12)) adder_1 (.a(controlled_buffer_3_out), .b(constant_1_p1), .out(adder_1_out));  // open: cin, cout
  // Pin pin_1: pin names not known; wires that end beside it: pin_1_p1
  // Pin pin_2: pin names not known; wires that end beside it: pin_2_p1
  // Pin pin_3: pin names not known; wires that end beside it: pin_3_p1
  // Pin pin_4: pin names not known; wires that end beside it: pin_4_p1
  assign controlled_buffer_1_out = pin_1_p1 ? adder_1_out : 12'bz;  // Controlled_Buffer controlled_buffer_1
  assign controlled_buffer_1_out = pin_6_p1 ? pin_2_p1 : 12'bz;  // Controlled_Buffer controlled_buffer_2
  assign controlled_buffer_3_out = pin_1_p1 ? register_1_q : 12'bz;  // Controlled_Buffer controlled_buffer_3
  Register #(.width(12), .trigger("falling")) register_1 (
    .D(controlled_buffer_1_out), .Q(register_1_q), .clk(pin_3_p1), .clr(pin_4_p1));  // open: en
  // Pin pin_5: pin names not known; wires that end beside it: register_1_q
  assign controlled_buffer_4_out = pin_7_p1 ? register_1_q : 12'bz;  // Controlled_Buffer controlled_buffer_4
  // Pin pin_6: pin names not known; wires that end beside it: pin_6_p1
  // Pin pin_7: pin names not known; wires that end beside it: pin_7_p1
  // Pin pin_8: pin names not known; wires that end beside it: controlled_buffer_4_out
endmodule

module AC (
);

  wire pin_3_p1, pin_4_p1, pin_5_p1, pin_6_p1;
  wire [15:0] controlled_buffer_1_out, controlled_buffer_2_out, multiplexer_1_out, pin_1_p1, pin_2_p1,
       register_1_q;

  // Pin pin_1: pin names not known; wires that end beside it: pin_1_p1
  // Pin pin_2: pin names not known; wires that end beside it: pin_2_p1
  // Pin pin_3: pin names not known; wires that end beside it: pin_3_p1
  assign controlled_buffer_1_out = pin_3_p1 ? pin_2_p1 : 16'bz;  // Controlled_Buffer controlled_buffer_1
  Multiplexer #(.width(16)) multiplexer_1 (
    .in0(pin_1_p1), .in1(controlled_buffer_1_out), .out(multiplexer_1_out), .sel(pin_3_p1));  // open: en
  // Pin pin_4: pin names not known; wires that end beside it: pin_4_p1
  // Pin pin_5: pin names not known; wires that end beside it: pin_5_p1
  Register #(.width(16), .trigger("falling")) register_1 (
    .D(multiplexer_1_out), .Q(register_1_q), .clk(pin_4_p1), .clr(pin_5_p1));  // open: en
  // Pin pin_6: pin names not known; wires that end beside it: pin_6_p1
  // Pin pin_7: pin names not known; wires that end beside it: register_1_q
  assign controlled_buffer_2_out = pin_6_p1 ? register_1_q : 16'bz;  // Controlled_Buffer controlled_buffer_2
  // Pin pin_8: pin names not known; wires that end beside it: controlled_buffer_2_out
endmodule

module TMP (
);

  wire pin_2_p1, pin_3_p1, pin_4_p1;
  wire [15:0] controlled_buffer_1_out, controlled_buffer_2_out, pin_1_p1, register_1_q;

  // Pin pin_1: pin names not known; wires that end beside it: pin_1_p1
  assign controlled_buffer_1_out = pin_2_p1 ? pin_1_p1 : 16'bz;  // Controlled_Buffer controlled_buffer_1
  // Pin pin_2: pin names not known; wires that end beside it: pin_2_p1
  // Pin pin_3: pin names not known; wires that end beside it: pin_3_p1
  Register #(.width(16), .trigger("falling")) register_1 (
    .D(controlled_buffer_1_out), .Q(register_1_q), .clk(pin_3_p1));  // open: en, clr
  // Pin pin_4: pin names not known; wires that end beside it: pin_4_p1
  // Pin pin_5: pin names not known; wires that end beside it: register_1_q
  assign controlled_buffer_2_out = pin_4_p1 ? register_1_q : 16'bz;  // Controlled_Buffer controlled_buffer_2
  // Pin pin_6: pin names not known; wires that end beside it: controlled_buffer_2_out
endmodule
